// Logisim project JK.circ as structural Verilog: 1 circuit, main circuit main
module main (
  input  J,
  input  K,
  input  Set,
  input  Enable,
  input  Reset,
  output Q,
  output Q_2
);

  wire clock_1_out;

  Clock clock_1 (.out(clock_1_out));
  J_K_Flip_Flop Biestable_JK (
    .J(J), .clk(clock_1_out), .K(K), .Q(Q), .Qn(Q_2), .preset(Set), .en(Enable), .reset(Reset));

  // Notes on the sheet:
  //   CLK
endmodule
