// Logisim project RS.circ as structural Verilog: 2 circuits, main circuit LatchRS
module LatchRS (
  input  S,
  input  R,
  output Q,
  output Q_2
);

  nand nand_1 (Q, S, Q_2);
  nand nand_2 (Q_2, Q, R);

  // Notes on the sheet:
  //   Latch RS
endmodule

module BiestableRs (
  input  S,
  input  R,
  output Q,
  output Q_2
);

  wire clock_1_out, nand_1_out, nand_2_out;

  Clock clock_1 (.out(clock_1_out));
  nand nand_1 (nand_1_out, S, clock_1_out);
  nand nand_2 (nand_2_out, clock_1_out, R);
  nand nand_3 (Q, nand_1_out, Q_2);
  nand nand_4 (Q_2, Q, nand_2_out);

  // Notes on the sheet:
  //   Biestable RS
endmodule
