// Logisim project RegistroParalelo.circ as structural Verilog: 1 circuit, main circuit main
module main (
  input  D2,
  input  D1,
  input  Desplaza_nCarga,
  input  D0,
  input  S,
  input  E,
  input  R,
  output LED_0,
  output LED_1,
  output LED_2
);

  wire CLK_out, G0_out, G1_out, G2_out, G3_out, not_1_out, or_1_out, or_2_out;

  Clock CLK (.out(CLK_out));
  not not_1 (not_1_out, Desplaza_nCarga);
  D_Flip_Flop u_D0 (.clk(CLK_out), .D(D0), .Q(LED_0), .preset(S), .en(E), .reset(R));  // open: Qn
  and G0 (G0_out, LED_0, Desplaza_nCarga);
  or or_1 (or_1_out, G0_out, G2_out);
  and G2 (G2_out, D1, not_1_out);
  D_Flip_Flop u_D1 (.clk(CLK_out), .D(or_1_out), .Q(LED_1), .preset(S), .en(E), .reset(R));  // open: Qn
  and G1 (G1_out, LED_1, Desplaza_nCarga);
  or or_2 (or_2_out, G1_out, G3_out);
  and G3 (G3_out, D2, not_1_out);
  D_Flip_Flop u_D2 (.clk(CLK_out), .D(or_2_out), .Q(LED_2), .preset(S), .en(E), .reset(R));  // open: Qn

  // Notes on the sheet:
  //   Registro de desplazamiento con Carga en Paralelo
endmodule
