// Logisim project RegistroSerie.circ as structural Verilog: 1 circuit, main circuit main
module main (
  input  D0,
  input  S,
  input  E,
  input  R,
  output QA,
  output QB,
  output QC,
  output QD
);

  wire CLK_out;

  Clock CLK (.out(CLK_out));
  D_Flip_Flop A (.clk(CLK_out), .D(D0), .Q(QA), .preset(S), .en(E), .reset(R));  // open: Qn
  D_Flip_Flop B (.clk(CLK_out), .D(QA), .Q(QB), .preset(S), .en(E), .reset(R));  // open: Qn
  D_Flip_Flop C (.clk(CLK_out), .D(QB), .Q(QC), .preset(S), .en(E), .reset(R));  // open: Qn
  D_Flip_Flop D (.clk(CLK_out), .D(QC), .Q(QD), .preset(S), .en(E), .reset(R));  // open: Qn

  // Notes on the sheet:
  //   Registro de Desplazamiento en Serie
endmodule
